# Fritzing sketch NodeBodyControl (saved by Fritzing 0.9.3b)

parts:
  Part1 = BluePill
  xinhan = Toggle Switch [package=THT]
  R8 = Resistor [tolerance=±5% resistance=1k package="1206 [SMD]"]
  R9 = Resistor [tolerance=±5% resistance=1k package="1206 [SMD]"]
  R10 = Resistor [tolerance=±5% resistance=1k package="1206 [SMD]"]
  R11 = Resistor [tolerance=±5% resistance=1k package="1206 [SMD]"]
  R12 = Resistor [tolerance=±5% resistance=1k package="1206 [SMD]"]
  Part2 = Black Joystick KY-023
  M1 = Niren can bus module [package=THT]
  SET_/_- = SWITCH-MOMENTARY-2 [package=tactile-pth-12mm]
  RES_/_+ = SWITCH-MOMENTARY-2 [package=tactile-pth-12mm]
  LIMIT = SWITCH-MOMENTARY-2 [package=tactile-pth-12mm]
  104 = Capacitor [package=cap-pth-small2]
  R14 = Resistor [tolerance=±5% resistance=10k package=THT]
  R15 = Resistor [tolerance=±5% resistance=10k package=THT]
  R16 = Resistor [tolerance=±5% resistance=10k package=THT]
  hazard = SWITCH-MOMENTARY-2 [package=tactile-pth-12mm]
  denpha = SWITCH-MOMENTARY-2 [package=tactile-pth-12mm]
  dencos = SWITCH-MOMENTARY-2 [package=tactile-pth-12mm]
  104_2 = Capacitor [package=cap-pth-small2]
  104_3 = Capacitor [package=cap-pth-small2]
  104_4 = Capacitor [package=cap-pth-small2]
  104_5 = Capacitor [package=cap-pth-small2]
  104_6 = Capacitor [package=cap-pth-small2]

nets:
  N1: Part1.A0, Part2.SW
  N2: Part1.A1, Part2.VRx
  N3: Part1.A4, M1.pin3
  N4: Part1.A5, M1.pin6
  N5: Part1.A6, M1.pin4
  N6: Part1.A7, M1.pin5
  N7: Part1.B0, R14.Pin_1
  N8: Part1.B10, R16.Pin_1
  N9: Part1.B11, R11.Pin_0
  N10: Part1.GND2, SET_/_-.1, RES_/_+.1, LIMIT.1, 104.1, hazard.1, denpha.1, 104_2.1, 104_3.1, 104_5.1, 104_6.1
  GND3: Part1.GND3, Part2.GND, M1.pin2
  5V: Part1.5V, Part2.+5V, M1.pin1
  N11: Part1.B12, R12.Pin_0
  N12: Part1.B1, R15.Pin_1
  N13: Part1.A2, Part2.VRy
  N14: xinhan.L1, R12.Pin_1
  N15: xinhan.COM, dencos.1, 104_4.1
  N16: xinhan.L2, R11.Pin_1
  N17: R8.Pin_0, hazard.2, 104_6.2
  N18: R9.Pin_0, denpha.2, 104_5.2
  N19: R10.Pin_0, dencos.2, 104_4.2
  N20: SET_/_-.2, 104.2, R14.Pin_0
  N21: RES_/_+.2, R15.Pin_0, 104_2.2
  N22: LIMIT.2, R16.Pin_0, 104_3.2

custom parts:
  Black Joystick KY-023: Description: The joystick is a combination of 2 analoog potentiometer and a digital switch. Arduino GND --> Module pin - Arduino +5V --> Module pin +5V Arduino Analoog 0 --> Module VRx Arduino Analoog 1 --> Module VRy Arduino Digital --> Module SW Dimensions: 1" x 1.25"
  Niren can bus module: Niren can bus module availabe on ebay and others. Pcb view assumes that you unsolder the 7 pin header and resolder it on the bottom of the module to connect to the pcb. The two jumpers and the can bus connector remain on the top of the board and don't appear in pcb view.
