# Fritzing sketch NodeReceive (saved by Fritzing 0.9.3b)

parts:
  Part1 = ESP-WROOM-32 [ESP-32S] Module [part_number=ESP-WROOM-32]
  M1 = Niren can bus module [package=THT]
  JP1 = Header 2 [package=jst-2-smd]
  JP2 = Header 4 [package=1x04-1mm-ra]
  U1 = BUTTON-CONDUCTIVE [package=button-conductive-0.1]
  R1 = Resistor [tolerance=±5% resistance=1k package="2512 [SMD]"]
  R2 = Resistor [tolerance=±5% resistance=1k package="2512 [SMD]"]
  U2 = BUTTON-CONDUCTIVE [package=button-conductive-0.1]

nets:
  N1: Part1.GND#0, M1.pin12
  N2: Part1.3V3, JP2.1, R1.Pin_0, R2.Pin_0
  N3: Part1.EN, R2.Pin_1, U2.2
  N4: Part1.GND#50, M1.pin2, JP1.2, JP2.4, U1.1, U2.1
  N5: Part1.IO0, U1.2, R1.Pin_1
  N6: Part1.IO5, M1.pin3
  N7: Part1.IO18, M1.pin6
  N8: Part1.IO19, M1.pin4
  N9: Part1.RXD0, JP2.3
  N10: Part1.TXD0, JP2.2
  N11: Part1.IO23, M1.pin5
  N12: M1.pin1, JP1.1

custom parts:
  ESP-WROOM-32 [ESP-32S] Module: Espressif ESP-WROOM-32 WiFi/Bluetooth LE microcontroller module also known as the Ai-Thinker ESP-32S module with similar formfactor. The ESP32 is a microcontroller chip with WiFi and BLE capabilities. The chip is developed by Espressif and is the successor to the popular ESP8266 WiFi module.
  Niren can bus module: Niren can bus module availabe on ebay and others. Pcb view assumes that you unsolder the 7 pin header and resolder it on the bottom of the module to connect to the pcb. The two jumpers and the can bus connector remain on the top of the board and don't appear in pcb view.
