# Fritzing sketch NodeSpeed (saved by Fritzing 0.9.3b)

parts:
  Part1 = BluePill
  M1 = Niren can bus module [package=THT]
  S1 = H-Bridge with L298N
  Part2 = FC-03 [chip_label=FC-03]
  VCC1 = Battery
  M2 = Getriebemotor
  Part3 = Motor Driver 1A Dual TB6612FNG
  Part4 = BluePill
  M3 = Niren can bus module [package=THT]
  Part5 = FC-03 [chip_label=FC-03]
  M4 = Getriebemotor
  VCC2 = Battery

nets:
  N1: Part1.A0, Part2.D0
  N2: Part1.A4, M1.pin3
  N3: Part1.A5, M1.pin6
  N4: Part1.A6, M1.pin4
  N5: Part1.A7, M1.pin5
  N6: Part1.3V31, Part2.VCC
  GND: Part1.GND3, M1.pin2, S1.GND, Part2.GND, VCC1.-
  5V: Part1.5V, M1.pin1, S1.5V
  N7: Part1.A11, S1.IN2
  N8: Part1.A10, S1.IN1
  N9: Part1.A9, S1.ENA
  N10: S1.12V, VCC1.+
  N11: S1.M1-01, M2.pin_2
  N12: S1.M1-02, M2.pin_1
  N13: Part3.A02, M4.pin_1
  N14: Part3.A01, M4.pin_2
  N15: Part3.GND, VCC2.-
  VCC: Part3.VCC, Part4.5V, M3.pin1
  N16: Part3.VM, VCC2.+
  N17: Part3.PWMA, Part4.A9
  N18: Part3.AIN2, Part4.A10
  N19: Part3.AIN1, Part4.A11
  N20: Part3.STBY, Part4.A12
  N21: Part4.A0, Part5.D0
  N22: Part4.A4, M3.pin3
  N23: Part4.A5, M3.pin6
  N24: Part4.A6, M3.pin4
  N25: Part4.A7, M3.pin5
  N26: Part4.3V31, Part5.VCC
  N27: Part4.GND3, M3.pin2

custom parts:
  Niren can bus module: Niren can bus module availabe on ebay and others. Pcb view assumes that you unsolder the 7 pin header and resolder it on the bottom of the module to connect to the pcb. The two jumpers and the can bus connector remain on the top of the board and don't appear in pcb view.
  H-Bridge with L298N: h-bridge
  FC-03: FC-03, LM393 IR Speed Sensor Encoder
